// Logisim project control-logic.circ as structural Verilog: 1 circuit, main circuit control_logic
module control_logic (
  input  [31:0] inst,
  input  BrEq,
  input  BrLt,
  output PCSel,
  output RegWEn,
  output [2:0] ImmSel,
  output BrUn,
  output ASel,
  output BSel,
  output [3:0] ALUSel,
  output MemRW,
  output [1:0] WBSel,
  output CSRSel,
  output CSRWen
);

  wire and_1_out, and_2_out, and_3_out, and_4_out, and_5_out, and_6_out, and_7_out, and_8_out, and_9_out,
       and_10_out, and_11_out, and_12_out, and_13_out, and_14_out, and_15_out, and_16_out, and_17_out,
       and_18_out, and_19_out, and_20_out, and_21_out, comparator_1_eq, comparator_2_eq, comparator_3_eq,
       comparator_4_eq, comparator_5_eq, comparator_6_eq, comparator_7_eq, comparator_8_eq, comparator_9_eq,
       comparator_10_eq, comparator_11_eq, comparator_12_eq, comparator_13_eq, comparator_14_eq,
       comparator_15_eq, comparator_16_eq, comparator_17_eq, comparator_18_eq, comparator_19_eq,
       comparator_20_eq, comparator_21_eq, comparator_21_gt, comparator_22_eq, comparator_23_eq,
       comparator_24_eq, comparator_25_eq, comparator_26_eq, comparator_27_eq, comparator_28_eq,
       comparator_29_eq, comparator_30_eq, not_1_out, not_2_out, not_3_out;
  wire [4:0] i, r, sb;
  wire [5:0] iinst, multiplexer_1_out;

  Multiplexer #(.enable("false"), .width(6)) multiplexer_1 (
    .in0({1'b0, i}), .in1({1'b0, r}), .out(multiplexer_1_out), .sel(comparator_1_eq));
  Comparator #(.width(7)) comparator_1 (.a(7'b0110011), .b(inst[6:0]), .eq(comparator_1_eq));  // open: gt, lt
  Comparator #(.width(7)) comparator_2 (.a(7'b1100011), .b(inst[6:0]), .eq(comparator_2_eq));  // open: gt, lt
  Comparator #(.mode("unsigned"), .width(3)) comparator_3 (
    .a(3'b000), .b(inst[14:12]), .eq(comparator_3_eq));  // open: gt, lt
  Comparator #(.mode("unsigned"), .width(3)) comparator_4 (
    .a(3'b001), .b(inst[14:12]), .eq(comparator_4_eq));  // open: gt, lt
  Comparator #(.mode("unsigned"), .width(3)) comparator_5 (
    .a(3'b010), .b(inst[14:12]), .eq(comparator_5_eq));  // open: gt, lt
  Comparator #(.mode("unsigned"), .width(3)) comparator_6 (
    .a(3'b100), .b(inst[14:12]), .eq(comparator_6_eq));  // open: gt, lt
  Comparator #(.mode("unsigned"), .width(3)) comparator_7 (
    .a(3'b101), .b(inst[14:12]), .eq(comparator_7_eq));  // open: gt, lt
  Comparator #(.mode("unsigned"), .width(3)) comparator_8 (
    .a(3'b110), .b(inst[14:12]), .eq(comparator_8_eq));  // open: gt, lt
  Comparator #(.mode("unsigned"), .width(3)) comparator_9 (
    .a(3'b111), .b(inst[14:12]), .eq(comparator_9_eq));  // open: gt, lt
  Comparator #(.mode("unsigned"), .width(3)) comparator_10 (
    .a(3'b000), .b(inst[14:12]), .eq(comparator_10_eq));  // open: gt, lt
  Comparator #(.mode("unsigned"), .width(3)) comparator_11 (
    .a(3'b001), .b(inst[14:12]), .eq(comparator_11_eq));  // open: gt, lt
  Comparator #(.mode("unsigned"), .width(3)) comparator_12 (
    .a(3'b010), .b(inst[14:12]), .eq(comparator_12_eq));  // open: gt, lt
  Comparator #(.mode("unsigned"), .width(3)) comparator_13 (
    .a(3'b011), .b(inst[14:12]), .eq(comparator_13_eq));  // open: gt, lt
  Comparator #(.mode("unsigned"), .width(3)) comparator_14 (
    .a(3'b100), .b(inst[14:12]), .eq(comparator_14_eq));  // open: gt, lt
  Comparator #(.mode("unsigned"), .width(3)) comparator_15 (
    .a(3'b101), .b(inst[14:12]), .eq(comparator_15_eq));  // open: gt, lt
  Comparator #(.mode("unsigned"), .width(3)) comparator_16 (
    .a(3'b110), .b(inst[14:12]), .eq(comparator_16_eq));  // open: gt, lt
  Comparator #(.mode("unsigned"), .width(3)) comparator_17 (
    .a(3'b111), .b(inst[14:12]), .eq(comparator_17_eq));  // open: gt, lt
  Comparator #(.mode("unsigned"), .width(7)) comparator_18 (
    .a(7'b0110011), .b(inst[6:0]), .eq(comparator_18_eq));  // open: gt, lt
  Comparator #(.mode("unsigned"), .width(7)) comparator_19 (
    .a(7'b1100011), .b(inst[6:0]), .eq(comparator_19_eq));  // open: gt, lt
  Multiplexer #(.enable("false"), .width(6)) multiplexer_2 (
    .in0(multiplexer_1_out), .in1({1'b0, sb}), .out(iinst), .sel(comparator_2_eq));
  Comparator #(.mode("unsigned"), .width(7)) comparator_20 (
    .a(7'b0010011), .b(inst[6:0]), .eq(comparator_20_eq));  // open: gt, lt
  Comparator #(.mode("unsigned"), .width(2)) comparator_21 (
    .a(inst[31:30]), .b(2'b00), .gt(comparator_21_gt), .eq(comparator_21_eq));  // open: lt
  Comparator #(.mode("unsigned"), .width(7)) comparator_22 (
    .a({7{1'b0}}), .b(inst[31:25]), .eq(comparator_22_eq));  // open: gt, lt
  Comparator #(.mode("unsigned"), .width(7)) comparator_23 (
    .a(7'b0000001), .b(inst[31:25]), .eq(comparator_23_eq));  // open: gt, lt
  Comparator #(.mode("unsigned"), .width(7)) comparator_24 (
    .a(7'b0100000), .b(inst[31:25]), .eq(comparator_24_eq));  // open: gt, lt
  Comparator #(.mode("unsigned"), .width(3)) comparator_25 (
    .a(inst[14:12]), .b(3'b000), .eq(comparator_25_eq));  // open: gt, lt
  Comparator #(.mode("unsigned"), .width(3)) comparator_26 (
    .a(inst[14:12]), .b(3'b001), .eq(comparator_26_eq));  // open: gt, lt
  Comparator #(.mode("unsigned"), .width(3)) comparator_27 (
    .a(inst[14:12]), .b(3'b100), .eq(comparator_27_eq));  // open: gt, lt
  Comparator #(.mode("unsigned"), .width(3)) comparator_28 (
    .a(inst[14:12]), .b(3'b101), .eq(comparator_28_eq));  // open: gt, lt
  Comparator #(.mode("unsigned"), .width(3)) comparator_29 (
    .a(inst[14:12]), .b(3'b110), .eq(comparator_29_eq));  // open: gt, lt
  Comparator #(.mode("unsigned"), .width(3)) comparator_30 (
    .a(inst[14:12]), .b(3'b111), .eq(comparator_30_eq));  // open: gt, lt
  ROM #(.addrWidth(6), .dataWidth(16)) rom_1 (
    .addr(iinst), .data({RegWEn, ImmSel, BrUn, ASel, BSel, ALUSel, MemRW, WBSel, CSRSel, CSRWen}));
  and and_1 (and_1_out, comparator_7_eq, comparator_21_eq);
  and and_2 (and_2_out, comparator_7_eq, comparator_21_gt);
  and and_3 (and_3_out, comparator_11_eq, comparator_22_eq);
  and and_4 (and_4_out, comparator_11_eq, comparator_23_eq);
  and and_5 (and_5_out, comparator_15_eq, comparator_22_eq);
  and and_6 (and_6_out, comparator_15_eq, comparator_24_eq);
  and and_7 (and_7_out, comparator_19_eq, comparator_25_eq);
  and and_8 (and_8_out, comparator_19_eq, comparator_26_eq);
  and and_9 (and_9_out, comparator_19_eq, comparator_27_eq);
  and and_10 (and_10_out, comparator_19_eq, comparator_28_eq);
  and and_11 (and_11_out, comparator_19_eq, comparator_29_eq);
  and and_12 (and_12_out, comparator_19_eq, comparator_30_eq);
  Priority_Encoder #(.select(5)) priority_encoder_1 (
    .in15(comparator_3_eq), .in16(comparator_4_eq), .in17(comparator_5_eq), .in18(comparator_6_eq),
    .in19(and_1_out), .in20(and_2_out), .in21(comparator_8_eq), .in22(comparator_9_eq), .out(i),
    .en_in(comparator_20_eq));  // open: in0, in1, in2, in3, in4, in5, in6, in7, in8, in9, in10, in11, in12, in13, in14, in23, in24, in25, in26, in27, in28, in29, in30, in31, gs, en_out
  not not_1 (not_1_out, BrLt);
  not not_2 (not_2_out, BrEq);
  not not_3 (not_3_out, BrLt);
  and and_13 (and_13_out, comparator_10_eq, comparator_22_eq);
  and and_14 (and_14_out, comparator_10_eq, comparator_23_eq);
  and and_15 (and_15_out, comparator_10_eq, comparator_24_eq);
  Priority_Encoder #(.select(5)) priority_encoder_2 (
    .in0(and_13_out), .in1(and_14_out), .in2(and_15_out), .in3(and_3_out), .in4(and_4_out),
    .in5(comparator_13_eq), .in6(comparator_12_eq), .in7(comparator_14_eq), .in8(and_5_out), .in9(and_6_out),
    .in10(comparator_16_eq), .in11(comparator_17_eq), .out(r), .en_in(comparator_18_eq));  // open: in12, in13, in14, in15, in16, in17, in18, in19, in20, in21, in22, in23, in24, in25, in26, in27, in28, in29, in30, in31, gs, en_out
  and and_16 (and_16_out, and_7_out, BrEq);
  and and_17 (and_17_out, and_8_out, not_2_out);
  and and_18 (and_18_out, and_9_out, BrLt);
  and and_19 (and_19_out, and_10_out, not_3_out);
  and and_20 (and_20_out, and_11_out, BrLt);
  and and_21 (and_21_out, and_12_out, not_1_out);
  Priority_Encoder #(.select(5)) priority_encoder_3 (
    .in26(and_7_out), .in27(and_8_out), .in28(and_9_out), .in29(and_10_out), .in30(and_11_out),
    .in31(and_12_out), .out(sb), .en_in(comparator_19_eq));  // open: in0, in1, in2, in3, in4, in5, in6, in7, in8, in9, in10, in11, in12, in13, in14, in15, in16, in17, in18, in19, in20, in21, in22, in23, in24, in25, gs, en_out
  or or_1 (BrUn, and_11_out, and_12_out);
  or or_2 (PCSel, and_16_out, and_17_out, and_18_out, and_19_out, and_20_out, and_21_out);

  // Other names for the same wires on the sheet: opcode[6:0] = inst[6:0]

  // Notes on the sheet:
  //   INPUTS to your circuit
  //   contents of rom_1 (hex, n*v repeats v):
  //   8004 8104 8184 8024 8124 8164 8044 8084 80a4 81a4 80c4 80e4 0 0 8200 8204 8224 8244 8284 82a4 83a4
  //   82c4 82e4 0 0 0 4*1604 1e04 1e04
  //   ROM FOR CONTROL LOGIC
  //   DON'T CHANGE THE LOCATIONS OF THE INPUTS AND OUTPUTS!
  //   OUTPUT from your circuit
  //   Reminder: Use combinational logic for PCSel
endmodule
