// Logisim project cpu.circ as structural Verilog: 1 circuit, main circuit cpu
module cpu (
  input  clk,
  input  [31:0] INSTRUCTION,
  input  [31:0] MEM_READ_DATA,
  output [31:0] MEM_WRITE_ADDRESS,
  output [31:0] PROGRAM_COUNTER,
  output [31:0] ra,
  output [31:0] sp,
  output [31:0] t0,
  output [31:0] t1,
  output [31:0] t2,
  output [31:0] s0,
  output [31:0] s1,
  output [31:0] a0,
  output [31:0] tohost,
  output [3:0] MEM_WRITE_ENABLE,
  output [31:0] MEM_WRITE_DATA
);

  wire branch_comp_1_breq, branch_comp_1_brlt, control_logic_1_asel, control_logic_1_brun,
       control_logic_1_bsel, control_logic_1_pcsel;
  wire [2:0] control_logic_1_immsel;
  wire [3:0] control_logic_1_alusel;
  wire [7:0] multiplexer_4_out, multiplexer_5_out, multiplexer_7_out;
  wire [15:0] multiplexer_6_out;
  wire [31:0] adder_1_out, alu_1_result, bit_extender_1_out, bit_extender_2_out, imm, multiplexer_1_out,
       multiplexer_2_out, multiplexer_3_out, multiplexer_8_out, multiplexer_9_out, regfile_1_read_data_1,
       regfile_1_read_data_2;

  Adder #(.width(32)) adder_1 (.a(PROGRAM_COUNTER), .b(32'h4), .out(adder_1_out));  // open: cin, cout
  Multiplexer #(.enable("false"), .width(32)) multiplexer_1 (
    .in0(adder_1_out), .in1(alu_1_result), .out(multiplexer_1_out), .sel(control_logic_1_pcsel));
  Register #(.width(32)) PC (.D(multiplexer_1_out), .clk(clk), .Q(PROGRAM_COUNTER));  // open: en, clr
  imm_gen imm_gen_1 (.inst(INSTRUCTION), .ImmSel(control_logic_1_immsel), .imm(imm));
  control_logic control_logic_1 (
    .PCSel(control_logic_1_pcsel), .ImmSel(control_logic_1_immsel), .BrUn(control_logic_1_brun),
    .ASel(control_logic_1_asel), .BSel(control_logic_1_bsel), .ALUSel(control_logic_1_alusel),
    .inst(INSTRUCTION), .BrEq(branch_comp_1_breq), .BrLt(branch_comp_1_brlt));  // open: CSRWen, RegWEn, MemRW, WBSel, CSRSel
  regfile regfile_1 (
    .rs1(INSTRUCTION[19:15]), .rs2(INSTRUCTION[24:20]), .rd(INSTRUCTION[11:7]), .Write_Data(alu_1_result),
    .RegWEn(1'b1), .clk(clk), .ra(ra), .sp(sp), .t0(t0), .t1(t1), .t2(t2), .s0(s0), .s1(s1), .a0(a0),
    .Read_Data_1(regfile_1_read_data_1), .Read_Data_2(regfile_1_read_data_2));
  branch_comp branch_comp_1 (
    .rs1(regfile_1_read_data_1), .rs2(regfile_1_read_data_2), .BrUn(control_logic_1_brun),
    .BrEq(branch_comp_1_breq), .BrLt(branch_comp_1_brlt));
  Multiplexer #(.enable("false"), .width(32)) multiplexer_2 (
    .in0(regfile_1_read_data_1), .in1(PROGRAM_COUNTER), .out(multiplexer_2_out), .sel(control_logic_1_asel));
  Multiplexer #(.enable("false"), .width(32)) multiplexer_3 (
    .in0(regfile_1_read_data_2), .in1(imm), .out(multiplexer_3_out), .sel(control_logic_1_bsel));
  alu alu_1 (.Result(alu_1_result), .A(multiplexer_2_out), .B(multiplexer_3_out), .ALUSel(control_logic_1_alusel));
  // csr csr_1: pin names not known; wires that end beside it: clk, tohost
  Multiplexer #(.enable("false"), .width(8)) multiplexer_4 (
    .in0(MEM_READ_DATA[7:0]), .in1(MEM_READ_DATA[15:8]), .out(multiplexer_4_out), .sel(MEM_WRITE_ADDRESS[0]));
  Multiplexer #(.enable("false"), .width(8)) multiplexer_5 (
    .in0(MEM_READ_DATA[23:16]), .in1(MEM_READ_DATA[31:24]), .out(multiplexer_5_out),
    .sel(MEM_WRITE_ADDRESS[0]));
  Multiplexer #(.enable("false"), .width(16)) multiplexer_6 (
    .in0(MEM_READ_DATA[15:0]), .in1(MEM_READ_DATA[31:16]), .out(multiplexer_6_out), .sel(MEM_WRITE_ADDRESS[1]));
  Multiplexer #(.enable("false"), .width(8)) multiplexer_7 (
    .in0(multiplexer_4_out), .in1(multiplexer_5_out), .out(multiplexer_7_out), .sel(MEM_WRITE_ADDRESS[1]));
  assign bit_extender_1_out = {{16{multiplexer_6_out[15]}}, multiplexer_6_out};  // Bit_Extender bit_extender_1
  assign bit_extender_2_out = {{24{multiplexer_7_out[7]}}, multiplexer_7_out};  // Bit_Extender bit_extender_2
  Multiplexer #(.enable("false"), .width(32)) multiplexer_8 (
    .in0(bit_extender_2_out), .in1(bit_extender_1_out), .out(multiplexer_8_out), .sel(INSTRUCTION[12]));
  Multiplexer #(.enable("false"), .width(32)) multiplexer_9 (
    .in0(multiplexer_8_out), .in1(MEM_READ_DATA), .out(multiplexer_9_out), .sel(INSTRUCTION[13]));

  // Other names for the same wires on the sheet: rd[4:0] = INSTRUCTION[11:7]; funct3[2:0] = INSTRUCTION[14:12];
  //   rs1[4:0] = INSTRUCTION[19:15]; rs2[4:0] = INSTRUCTION[24:20]

  // Notes on the sheet:
  //   Output to IMEM
  //   IMEM (do **NOT** move this)
  //   Inputs from IMEM
  //   It is OK to move the PC, RegFile, ALU, MEM, Branch Comp, Imm Gen, and Control Logic to wherever is most convenient for you when constructing your CPU, and to delete this text
  //   Inputs/Outputs for testing. Do **NOT** move these.
  //   Outputs To DMEM
  //   DMEM (do **NOT** move this)
  //   Inputs From DMEM
endmodule
